# Fritzing sketch Gravity Car (saved by Fritzing 0.9.3b)
breadboards: 1

parts:
  Componente1 = Arduino Uno (Rev3) - ICSP
  U1 = POT [package=pot_alpha_rv16af-20]
  U2 = POT [package=pot_alpha_rv16af-20]
  U3 = POT [package=pot_alpha_rv16af-20]
  Componente2 = Bluetooth HC-05 Macho
  R1 = Resistor [tolerance=±5% resistance=680 package=THT]
  R2 = Resistor [tolerance=±5% resistance=470 package=THT]
  LED1 = LED - 3mm [color="Red (633nm)" package="3 mm [THT]"]
  R4 = Resistor [tolerance=±5% resistance=270 package="0402 [SMD]"]
  LED2 = LED - 3mm [color="Red (633nm)" package="3 mm [THT]"]
  LED3 = LED - 3mm [color="Red (633nm)" package="3 mm [THT]"]
  LED4 = LED - 3mm [color="Red (633nm)" package="3 mm [THT]"]
  R5 = Resistor [tolerance=±5% resistance=270 package="0402 [SMD]"]
  R6 = Resistor [tolerance=±5% resistance=270 package="0402 [SMD]"]
  R7 = Resistor [tolerance=±5% resistance=270 package="0402 [SMD]"]
  M7 = DC Motor  # not connected
  M8 = DC Motor  # not connected
  M9 = DC Motor  # not connected
  M10 = DC Motor  # not connected
  M11 = DC Motor  # not connected
  M17 = DC Motor  # not connected
  M18 = DC Motor  # not connected
  M19 = DC Motor  # not connected
  M20 = DC Motor  # not connected
  M21 = DC Motor  # not connected
  M22 = DC Motor  # not connected
  M23 = DC Motor  # not connected

nets:
  N1: Componente1.A0, U3.S
  N2: Componente1.A1, U2.S
  N3: Componente1.A2, U1.S
  N4: Componente1.D0/RX, Componente2.TXD
  N5: Componente1.D1/TX, R2.Pin_0
  5V: Componente1.5V, U1.E, U2.E, U3.E, Componente2.VCC, LED4.cathode
  GND: Componente1.GND, U1.A, U2.A, U3.A, Componente2.GND, R1.Pin_1, R4.Pin_0, R5.Pin_0, R6.Pin_0, R7.Pin_0
  N6: Componente2.RXD, R1.Pin_0, R2.Pin_1
  N7: LED1.anode, R5.Pin_1
  N8: R4.Pin_1, LED4.anode
  N9: LED2.anode, R6.Pin_1
  N10: LED3.anode, R7.Pin_1

notes:
  Left Motors
  Right Motors
